# Fritzing sketch Car Park Turnstile Fritzing Project (saved by Fritzing 0.9.3b)
breadboards: 1

parts:
  Part1 = Arduino Uno (Rev3) - ICSP
  Parça1 = SRF05 Ultrasonic Rangefinder
  J1 = Basic Servo
  U1 = RFID RC522 SIP - 8 pins [chip_label="RFID RC522" package="SIP (Single Inline) [THT]"]

nets:
  N1: Part1.ICSP_MISO, Part1.D12/MISO, U1.MOSI
  N2: Part1.D8, J1.pulse
  N3: Part1.D9_PWM, U1.RST
  N4: Part1.D10_PWM/SS, U1.IRQ
  N5: Part1.D11_PWM/MOSI, U1.SCK
  N6: Part1.D13/SCK, U1.NSS
  GND: Part1.GND, Parça1.GND, J1.gnd, U1.GND
  N7: Part1.D6_PWM, Parça1.Echo
  N8: Part1.D7, Parça1.Trig
  3V3: Part1.3V3, U1.VCC
  VCC: Part1.5V, Parça1.VCC, J1.vcc

custom parts:
  RFID RC522 SIP - 8 pins: A SIP stand-in part for RFID RC522 . With 8 pins on a 300 mil single inline package (SIP) footprint.
